# Fritzing sketch read-aloud_for_blind-layout (saved by Fritzing 0.9.3b)

parts:
  S1 = Pushbutton [package="[THT]"]
  CAMERA1 = TTL Serial JPEG Camera  # not connected
  Raspberry_Pi_1 = Raspberry Pi 3 [part_number=RPI-3-V1.2]
  SPKR1 = Loudspeaker  # not connected

nets:
  N1: S1.Pin_2, Raspberry_Pi_1.GND
  N2: S1.Pin_4, Raspberry_Pi_1.GPIO2

custom parts:
  TTL Serial JPEG Camera: TTL Serial JPEG Camera with NTSC Out
